# Fritzing sketch Schema Weather Station (saved by Fritzing 0.9.3b)
breadboards: 2

parts:
  Componente1 = Arduino Due (Rev2b)
  U1 = ESP8266 NodeMCU LoLin module
  Componente2 = Humidity Temperature Sensor SHT15
  S2 = Pushbutton [package="[SMD]"]
  R1 = Resistor [tolerance=±5% resistance=10k package="0603 [SMD]"]
  R2 = Resistor [tolerance=±5% resistance=4.7k package="0805 [SMD]"]
  LED1 = LED - 5mm [color="Green (565nm)" package="5 mm [THT]"]
  microSD1 = MicroSD Card Module

nets:
  N1: Componente1.D14/TX3, U1.D1
  N2: Componente1.D15/RX3, U1.D4
  N3: Componente1.D20/SDA3, Componente2.SDA
  N4: Componente1.D21/SCL3, Componente2.SCL
  N5: Componente1.IOREF, S2.Pin_3, S2.Pin_4
  VCC: Componente1.5V, Componente2.VCC, microSD1.VCC
  GND: Componente1.GND, U1.GND, Componente2.GND, R1.Pin_1, LED1.cathode, microSD1.GND
  N6: Componente1.D45, S2.Pin_1, S2.Pin_2, R1.Pin_0
  N7: U1.D2, R2.Pin_0
  N8: U1.D5, microSD1.SCK
  N9: U1.D6, microSD1.MISO
  N10: U1.D7, microSD1.MOSI
  N11: U1.D8, microSD1.CS
  N12: R2.Pin_1, LED1.anode

custom parts:
  ESP8266 NodeMCU LoLin module: ESP8266 based NodeMCU
